# Fritzing sketch photo-move (saved by Fritzing 1.0.5)
breadboards: 5

parts:
  Solar_Cell_1 = Solar Panel [package="80x80mm 6V 0.9W Solar Panel"]
  Solar_Cell_2 = Solar Panel [package="80x80mm 6V 0.9W Solar Panel"]
  Solar_Cell_3 = Solar Panel [package="80x80mm 6V 0.9W Solar Panel"]
  D1 = Schottky Diode [part_number=1N5817 package="300 mil [THT]"]
  D2 = Schottky Diode [part_number=1N5817 package="300 mil [THT]"]
  D3 = Schottky Diode [part_number=1N5817 package="300 mil [THT]"]
  A1 = CN3065 Mini Solar Charger Module
  LIPO_Battery = LIPO-2000mAh [package=lipo-2000]
  S1 = Toggle Switch [package=THT]
  Mod1 = YL-99 Limit switch and LED
  Mod2 = YL-99 Limit switch and LED
  Mod3 = YL-99 Limit switch and LED
  ULN1 = Darlington Driver [package=dil18]
  LED1 = smd LED [color="Red (633nm)" package="0805 [SMD]"]
  R1 = Resistor [tolerance=±5% power=0.25W resistance=470 package=THT]
  Pico/Pico2_Mod_1 = Raspberry Pi Pico or Pico 2
  A3 = mini boost module
  A4 = mini boost module
  LED3 = smd LED [color="Green (555nm)" package="0805 [SMD]"]
  R2 = Resistor [tolerance=±5% power=0.25W resistance=470 package=THT]
  LED4 = smd LED [color="Yellow (585nm)" package="0805 [SMD]"]
  R3 = Resistor [tolerance=±5% power=0.25W resistance=470 package=THT]
  D4 = Schottky Diode [part_number=1N5817 package="300 mil [THT]"]
  R4 = Resistor [tolerance=±5% power=0.25W resistance=220 package=THT]
  R5 = Resistor [tolerance=±5% power=0.25W resistance=220 package=THT]
  Mod4 = Micro SD Card Module
  Part3 = XBee USB Mini Adapter
  U3 = XBEE-1 [package=xbee-silk]  # not connected
  OLED1 = OLED 128x64 I2C Monochrome Display VDD-GND
  M1 = gy9250
  A5 = NEO-6M GPS Module [part_number=GY-GPS6MV2]
  A6 = Arducam Mega 3MP SPI Camera (OV5642)

nets (from the schematic view):
  N1: Solar_Cell_1.Connector_1, D3.anode
  N2: Solar_Cell_1.Connector_2, Solar_Cell_2.Connector_2, Solar_Cell_3.Connector_2
  N3: Solar_Cell_2.Connector_1, D2.anode
  N4: Solar_Cell_3.Connector_1, D1.anode
  N5: D1.cathode, D2.cathode, D3.cathode, A1.Pin_1, A1.Pin_3
  GND: A1.Pin_2, A1.Pin_4, A1.Pin_8, A1.Pin_10, LIPO_Battery.-, Mod1.GND, Mod2.GND, Mod3.GND, ULN1.9, Pico/Pico2_Mod_1.pin_3, Pico/Pico2_Mod_1.pin_8, Pico/Pico2_Mod_1.pin_13, Pico/Pico2_Mod_1.pin_18, Pico/Pico2_Mod_1.pin_23, Pico/Pico2_Mod_1.pin_28, Pico/Pico2_Mod_1.pin_33, Pico/Pico2_Mod_1.pin_38, Pico/Pico2_Mod_1.pin_42, R5.Pin_1
  N6: A1.Pin_7, A1.Pin_9, LIPO_Battery.+, S1.COM
  N7: S1.L2, Mod1.OUT
  N8: Mod1.VCC, Mod2.OUT
  N9: Mod2.VCC, Mod3.OUT
  N10: Mod3.VCC, ULN1.10, LED1.anode, A3.Pin_2, D4.anode, R4.Pin_0
  N11: ULN1.1, Pico/Pico2_Mod_1.pin_29
  N12: ULN1.18, R1.Pin_1, A3.Pin_1
  N13: LED1.cathode, R1.Pin_0
  N14: Pico/Pico2_Mod_1.pin_1, Part3.TXD
  N15: Pico/Pico2_Mod_1.pin_2, Part3.RXD
  N16: Pico/Pico2_Mod_1.pin_4, Part3.RST
  N17: Pico/Pico2_Mod_1.pin_6, A5.Rx
  N18: Pico/Pico2_Mod_1.pin_7, A5.Tx
  N19: Pico/Pico2_Mod_1.pin_9, OLED1.SDA
  N20: Pico/Pico2_Mod_1.pin_10, OLED1.SCK
  N21: Pico/Pico2_Mod_1.pin_14, Mod4.pin_11, Mod4.pin_12
  N22: Pico/Pico2_Mod_1.pin_15, Mod4.pin_9, Mod4.pin_10
  N23: Pico/Pico2_Mod_1.pin_16, Mod4.pin_13, Mod4.pin_14
  N24: Pico/Pico2_Mod_1.pin_17, Mod4.pin_7, Mod4.pin_8
  N25: Pico/Pico2_Mod_1.pin_21, A6.Pin_6
  N26: Pico/Pico2_Mod_1.pin_22, A6.Pin_8
  N27: Pico/Pico2_Mod_1.pin_24, A6.Pin_5
  N28: Pico/Pico2_Mod_1.pin_25, A6.Pin_7
  N29: Pico/Pico2_Mod_1.pin_26, M1.pin4
  N30: Pico/Pico2_Mod_1.pin_27, M1.pin3
  N31: Pico/Pico2_Mod_1.pin_34, R5.Pin_0
  N32: Pico/Pico2_Mod_1.pin_39, D4.cathode
  N33: A3.Pin_3, A4.Pin_1, R2.Pin_1
  N34: A3.Pin_4, A4.Pin_2, LED3.anode
  GND_2: A4.Pin_3, R3.Pin_1, Mod4.pin_1, Mod4.pin_2, Mod4.pin_15, Mod4.pin_16, Part3.GND, OLED1.GND, M1.pin2, A5.GND, A6.Pin_4
  5V: A4.Pin_4, LED4.anode, Mod4.pin_3, Mod4.pin_4, Part3.5V, OLED1.VDD, M1.pin1, A5.Vcc, A6.Pin_3

notes:
  SPI Camera
  Schottky diode to protect circuit from reverse flow of current
  XBee COM Module
  SD Card Module
  Limit and Mission Before Switches
  System Switch
  3.3 V DC to DC Buck Converter
  5 V DC to DC Boost Converter
  6V solar Panels
  3V3 Regulated Power Supply
  5V Regulated Power Supply
  Switched Unregulated Power Supply
  Unregulated Power Supply
  3.7 V LIPO 2000MAH
  Solar Charge Controller Module
  9 AXIS Sensor Module
  GPS Module

custom parts:
  Solar Panel: 80x80mm 6V 0.9W Solar Panel, 150mA, tested at 38000LUX
  CN3065 Mini Solar Charger Module: Fc-51 Infrared Obstacle Avoidance Proximity Sensor module. IR transmitter led, receiver LED, lm393 compaitor and a pot. 3.3 V to 5V power.
  Raspberry Pi Pico or Pico 2: Raspberry Pi Pico and Pico 2. Based around the RP2040 and RP2350 microcontrollers respectively, Picos are low cost microcontroller device bringing Raspberry Pi quality, cost, and easy of use to the microcontroller space. Jan 2021, Split part in to two versions: tht (this one) and SMD. This one will drill holes for a .1 in header in pcb to allow plugging in the module as well as providing pads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
  mini boost module: mini boost module.
  Micro SD Card Module: Micro SD Storage Board TF Card Reader Memory Shield Module SPI Port for Arduino
  OLED 128x64 I2C Monochrome Display VDD-GND: OLED 128x64 I2C Monochrome Display. Note: there are two variants of this part, this one is the VDD GND SCK SDA variant. The other is GND VDD SCK SDA. Make sure you select the part that matches your module as using the incorrect part will probably destroy your module! In addition the mounting holes are marked on silkscreen but not by default drilled. If you want drilled mounting holes, copy a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
  gy9250: MPU-9250 module (three-axis gyroscope + three-axis acceleration + three-axis magnetic field). The generic model from ebay et. al. rather than the Sparkfun version.
  NEO-6M GPS Module: GY-GPS6MV2 NEO-6M GPS Module Module based on U-blox NEO-6M GPS engine, incorporating regulator for 3.3-5V DC input, MS621FE-compatible rechargeable battery for backup and EEPROM for storing configuration settings. Links: NEO-6 series product information page NEO-6 Datasheet
  Arducam Mega 3MP SPI Camera (OV5642): Arducam Mega 3MP SPI camera is a 3-megapixel module (2048x1536) that uses an OV5642 sensor, features a 1/4" optical size, operates on 3.3V or 5V power, and communicates via a 4-wire SPI interface. It includes a rolling shutter, offers RGB/YUV/JPEG output formats, and has a fixed focal length of 3.3mm with a focusing distance from 6cm to infinity.
